# Fritzing sketch cookieboard (saved by Fritzing 0.9.4)
stripboards: 1

parts:
  ESP01S = ESP8266 WiFi Module [part_number=ESP8266]
  Pololu_A1 = Pololu A4988 [package=SO16]
  C8 = Electrolytic Capacitor [capacitance=1µF package="100 mil [THT, electrolytic]"]
  Power_plug3 = Power plug
  C9 = Electrolytic Capacitor [capacitance=1µF package="100 mil [THT, electrolytic]"]
  M1 = Stepper Motor - Bipolar
  MP1584EN_Board1 = MP1584EN Power Regulator Board [part_number=MP1584EN]
  S1 = Pushbutton [package="[SMD]"]

nets:
  N1: ESP01S.RXD, S1.Pin_1, S1.Pin_2
  VCC: ESP01S.VCC, Pololu_A1.VDD, C8.+, MP1584EN_Board1.OUT_+#16
  N2: ESP01S.GPIO_0, Pololu_A1.STEP
  N3: ESP01S.GPIO_2, Pololu_A1.DIR
  N4: ESP01S.GND, Pololu_A1.GND#8, C8.-, MP1584EN_Board1.OUT_-#13, S1.Pin_3, S1.Pin_4
  N5: ESP01S.TXD, Pololu_A1.ENABLE
  N6: Pololu_A1.RESET, Pololu_A1.SLEEP
  N7: Pololu_A1.1B, M1.D
  N8: Pololu_A1.1A, M1.B
  N9: Pololu_A1.2A, M1.C
  N10: Pololu_A1.2B, M1.A
  N11: Pololu_A1.GND#14, Power_plug3.GND, C9.-, MP1584EN_Board1.IN_-#9
  N12: Pololu_A1.VMOT, Power_plug3.VCC, C9.+, MP1584EN_Board1.IN_+

custom parts:
  ESP8266 WiFi Module: Generic WiFi Module based on the ESP8266 with onboard PCB antenna and UART communications
  MP1584EN Power Regulator Board: The MP1584EN is a high frequency step-down switching regulator. The input voltage range is 4.5V to 28V. The output voltage is set by the board's potentiometer.
